# Fritzing sketch led_running (saved by Fritzing 0.9.5d)
breadboards: 1

parts:
  元件1 = Arduino Uno (Rev3)
  LED1 = LED - 5mm [color="Red (633nm)" package="5 mm [THT]"]
  R1 = Resistor [tolerance=±5% resistance=220 package=THT]
  LED2 = LED - 5mm [color="Yellow (595nm)" package="5 mm [THT]"]
  LED3 = LED - 5mm [color="Green (555nm)" package="5 mm [THT]"]
  LED5 = LED - 5mm [color="Yellow (595nm)" package="5 mm [THT]"]
  LED6 = LED - 5mm [color="Green (555nm)" package="5 mm [THT]"]
  LED4 = LED - 5mm [color="Red (633nm)" package="5 mm [THT]"]
  R2 = Resistor [tolerance=±5% resistance=220 package=THT]
  R3 = Resistor [tolerance=±5% resistance=220 package=THT]
  R5 = Resistor [tolerance=±5% resistance=220 package=THT]
  R6 = Resistor [tolerance=±5% resistance=220 package=THT]
  R4 = Resistor [tolerance=±5% resistance=220 package=THT]

nets:
  N1: 元件1.GND, LED1.cathode, LED2.cathode, LED3.cathode, LED5.cathode, LED6.cathode, LED4.cathode
  N2: 元件1.D2, R6.Pin_0
  N3: 元件1.D3_PWM, R5.Pin_0
  N4: 元件1.D4, R4.Pin_0
  N5: 元件1.D5_PWM, R3.Pin_0
  N6: 元件1.D6_PWM, R2.Pin_0
  N7: 元件1.D7, R1.Pin_0
  N8: LED1.anode, R1.Pin_1
  N9: LED2.anode, R2.Pin_1
  N10: LED3.anode, R3.Pin_1
  N11: LED5.anode, R5.Pin_1
  N12: LED6.anode, R6.Pin_1
  N13: LED4.anode, R4.Pin_1
