# Fritzing sketch rgb_led (saved by Fritzing 0.9.5d)
breadboards: 1

parts:
  元件1 = Arduino Uno (Rev3)
  R1 = Resistor [tolerance=±5% resistance=220 package=THT]
  R2 = Resistor [tolerance=±5% resistance=220 package=THT]
  R3 = Resistor [tolerance=±5% resistance=220 package=THT]
  RGB-LED = RGB LED (com. cathode, rgb) [package="5 mm [THT]"]

nets:
  N1: 元件1.D9_PWM, R3.Pin_0
  N2: 元件1.D10_PWM/SS, R2.Pin_0
  N3: 元件1.D11_PWM/MOSI, R1.Pin_0
  N4: 元件1.GND, RGB-LED.common_cathode
  N5: R1.Pin_1, RGB-LED.blue_anode
  N6: R2.Pin_1, RGB-LED.green_anode
  N7: R3.Pin_1, RGB-LED.red_anode
